// Logisim project MicrocodedCPU.circ as structural Verilog: 8 circuits, main circuit main
module main (
  input  Reset
);

  wire alu_1_is, alu_1_is_2, aluEnable, aluResultRead, aluResultWrite, ARead, AWrite, branchTarget, BRead,
       BWrite, clock, flags_1_flags_e, flags_1_flags_gt, flags_E, flags_E_q, flags_GT, flags_GT_q, I_q, immx,
       ir, ldResultRead, ldResultWrite, marRead, marWrite, mdrRead, mdrWrite, MemEnable, pcRead, pcWrite, rd,
       regDataRead, regDataWrite, regEnable, regsrcRead, regSrcWrite, regValRead, regValWrite, rs1, rs2;
  wire [1:0] transfer;
  wire [3:0] rd_q, register_3_q, rs1_q, rs2_q;
  wire [4:0] IR_q_2, opcode;
  wire [5:0] args;
  wire [17:0] immx_q;
  wire [26:0] IR_q;
  wire [31:0] A_q, adder_1_out, adder_2_out, alu_1_aluresult, aluResult_q, B_q, bit_extender_1_out,
       bit_extender_2_out, bit_extender_3_out, bit_extender_4_out, bit_extender_5_out, bit_extender_6_out,
       bit_extender_7_out, branchTarget_q, controlled_buffer_1_out, immediate_unit_1_immx, ldResult_q,
       memory_1_ldresult, microImm, multiplexer_1_out, multiplexer_2_out, PC, register_1_q, register_2_q,
       rom_1_data, shifter_1_out, X;
  wire [31:4] register_3_q_2;

  MicroControl_Unit microcontrol_unit_1 (
    .readbusVal(multiplexer_2_out), .opcode(opcode), .Clock(clock), .microImm(microImm),
    .pc({pcWrite, pcRead}), .args(args), .microImm_readBusVal(X), .transfer(transfer), .ir(ir), .I(flags_GT),
    .rd(rd), .rs1(rs1), .rs2(rs2), .immx(immx), .branchTarget(branchTarget),
    .regSrc({regSrcWrite, regsrcRead}), .regData({regDataWrite, regDataRead}),
    .regVal({regValWrite, regValRead}), .A({AWrite, ARead}), .B({BWrite, BRead}), .flags_E(flags_E),
    .flags_GT(flags_GT), .aluResult({aluResultWrite, aluResultRead}), .mar({marWrite, marRead}),
    .mdr({mdrWrite, mdrRead}), .ldResult({ldResultWrite, ldResultRead}));
  Register #(.width(32), .trigger("falling")) u_PC (
    .D(multiplexer_1_out), .Q(PC), .clk(clock), .clr(Reset));  // open: en
  assign controlled_buffer_1_out = pcWrite ? PC : 32'bz;  // Controlled_Buffer controlled_buffer_1
  Multiplexer #(.width(32), .enable("false")) multiplexer_1 (
    .in0(multiplexer_2_out), .in1(adder_1_out), .out(multiplexer_1_out));  // open: sel
  Adder #(.width(32)) adder_1 (.a(PC), .b(32'h4), .out(adder_1_out));  // open: cin, cout
  Memory memory_1 (
    .MAR(multiplexer_2_out), .marRead(marRead), .MDR(multiplexer_2_out), .Clock(clock), .enable(MemEnable),
    .operation(args[5:2]), .mdrRead(mdrRead), .ldResult(memory_1_ldresult));
  assign controlled_buffer_1_out = ldResultWrite ? ldResult_q : 32'bz;  // Controlled_Buffer controlled_buffer_2
  Register #(.width(32), .trigger("falling")) ldResult (
    .D(memory_1_ldresult), .Q(ldResult_q), .clk(clock));  // open: en, clr
  ROM #(.addrWidth(24), .dataWidth(32)) rom_1 (.addr(PC[25:2]), .data(rom_1_data));  // open: sel
  Register #(.width(5), .trigger("falling")) u_opcode (.D(IR_q_2), .Q(opcode), .clk(clock));  // open: en, clr
  assign controlled_buffer_1_out = aluResultWrite ? aluResult_q : 32'bz;  // Controlled_Buffer controlled_buffer_3
  Register #(.width(32)) aluResult (.D(alu_1_aluresult), .en(ARead), .Q(aluResult_q), .clk(clock));  // open: clr
  Register #(.width(32), .trigger("falling")) u_IR (.D(rom_1_data), .Q({IR_q_2, IR_q}), .clk(clock));  // open: en, clr
  Register #(.width(32)) A (.D(multiplexer_2_out), .Q(A_q), .clk(clock));  // open: en, clr
  ALU alu_1 (
    .A(A_q), .B(B_q), .opcode(args[5:2]), .aluResult(alu_1_aluresult), .is(alu_1_is), .is_2(alu_1_is_2));  // open: Carry
  Clock u_Clock (.out(clock));
  assign controlled_buffer_1_out = ir ? {IR_q_2, IR_q} : 32'bz;  // Controlled_Buffer controlled_buffer_4
  Register #(.width(32)) B (.D(multiplexer_2_out), .en(BRead), .Q(B_q), .clk(clock));  // open: clr
  Flags flags_1 (
    .is(alu_1_is), .is_2(alu_1_is_2), .flags_GT(flags_1_flags_gt), .flags_E(flags_1_flags_e));  // open: isCmp
  Register #(.width(1), .trigger("falling")) I (.D(IR_q[26]), .Q(I_q), .clk(clock));  // open: en, clr
  Register #(.width(4), .trigger("falling")) u_rd (.D(IR_q[25:22]), .Q(rd_q), .clk(clock));  // open: en, clr
  assign bit_extender_1_out = {{31{1'b0}}, I_q};  // Bit_Extender bit_extender_1
  assign controlled_buffer_1_out = flags_GT ? bit_extender_1_out : 32'bz;  // Controlled_Buffer controlled_buffer_5
  assign controlled_buffer_1_out = flags_GT ? bit_extender_2_out : 32'bz;  // Controlled_Buffer controlled_buffer_6
  Register #(.width(1), .trigger("falling")) u_flags_GT (
    .D(flags_1_flags_gt), .Q(flags_GT_q), .clk(clock));  // open: en, clr
  Bit_Extender #(.in_width(1), .out_width(32)) bit_extender_2 (.out(bit_extender_2_out));  // open: in
  Register #(.width(1), .trigger("falling")) u_flags_E (.D(flags_1_flags_e), .Q(flags_E_q));  // open: en, clk, clr
  assign bit_extender_3_out = {{5{IR_q[26]}}, IR_q};  // Bit_Extender bit_extender_3
  Register #(.width(4), .trigger("falling")) u_rs1 (.D(IR_q[21:18]), .Q(rs1_q), .clk(clock));  // open: en, clr
  assign bit_extender_4_out = {{28{1'b0}}, rd_q};  // Bit_Extender bit_extender_4
  assign controlled_buffer_1_out = rd ? bit_extender_4_out : 32'bz;  // Controlled_Buffer controlled_buffer_7
  Register #(.width(32)) register_1 (
    .D(multiplexer_2_out), .en(regValRead), .Q(register_1_q), .clk(clock));  // open: clr
  assign controlled_buffer_1_out = flags_E ? bit_extender_5_out : 32'bz;  // Controlled_Buffer controlled_buffer_8
  assign bit_extender_5_out = {{31{1'b0}}, flags_E_q};  // Bit_Extender bit_extender_5
  Shifter #(.width(32)) shifter_1 (.in(bit_extender_3_out), .\dist (5'b00010), .out(shifter_1_out));
  Register #(.width(4), .trigger("falling")) u_rs2 (.D(IR_q[17:14]), .Q(rs2_q), .clk(clock));  // open: en, clr
  assign bit_extender_6_out = {{28{1'b0}}, rs1_q};  // Bit_Extender bit_extender_6
  assign bit_extender_7_out = {{28{1'b0}}, rs2_q};  // Bit_Extender bit_extender_7
  assign controlled_buffer_1_out = rs1 ? bit_extender_6_out : 32'bz;  // Controlled_Buffer controlled_buffer_9
  Register #(.width(32)) register_2 (
    .D(multiplexer_2_out), .en(regDataRead), .Q(register_2_q), .clk(clock));  // open: clr
  Register_file register_file_1 (
    .regData(register_2_q), .opcode(args[5:2]), .regSrc(register_3_q), .regVal(register_1_q));  // open: Clock, Reset, DisplayAddress, DisplayD
  Multiplexer #(.select(2), .width(32), .enable("false")) multiplexer_2 (
    .in0(microImm), .in1(X), .in2(controlled_buffer_1_out), .out(multiplexer_2_out), .sel(transfer));  // open: in3
  Decoder #(.select(2), .enable("false")) decoder_1 (
    .out0(aluEnable), .out1(regEnable), .out2(MemEnable), .sel(args[1:0]));  // open: out3
  Adder #(.width(32)) adder_2 (.a(shifter_1_out), .b(PC), .out(adder_2_out));  // open: cin, cout
  Register #(.width(18), .trigger("falling")) u_immx (.D(IR_q[17:0]), .Q(immx_q), .clk(clock));  // open: en, clr
  Immediate_Unit immediate_unit_1 (.imm(immx_q), .immx(immediate_unit_1_immx));
  assign controlled_buffer_1_out = rs2 ? bit_extender_7_out : 32'bz;  // Controlled_Buffer controlled_buffer_10
  Register #(.width(32)) register_3 (
    .D(multiplexer_2_out), .en(regsrcRead), .Q({register_3_q_2, register_3_q}), .clk(clock));  // open: clr
  Register #(.width(32), .trigger("falling")) u_branchTarget (
    .D(adder_2_out), .Q(branchTarget_q), .clk(clock));  // open: en, clr
  assign controlled_buffer_1_out = immx ? immediate_unit_1_immx : 32'bz;  // Controlled_Buffer immx_out
  assign controlled_buffer_1_out = branchTarget ? branchTarget_q : 32'bz;  // Controlled_Buffer bTout

  // Other names for the same wires on the sheet: operation[3:0] = args[5:2]; I = flags_GT

  // Notes on the sheet:
  //   Microcode Logic
  //   Micro Processor
  //   Data Memory
  //   Instruction Memory
  //   ALU
  //   flags
  //   regVal
  //   regData
  //   Register File
  //   readBus
  //   regSrc
  //   writeBus
endmodule

module ALU (
  input  Carry,
  input  [31:0] A,
  input  [31:0] B,
  input  [3:0] opcode,
  output [31:0] aluResult,
  output is,
  output is_2
);

  wire adder_1_cout, subtractor_1_bout;
  wire [31:0] adder_1_out, and_1_out, divider_1_out, divider_1_rem, multiplier_1_out, not_1_out, or_1_out,
       shifter_1_out, shifter_2_out, shifter_3_out, subtractor_1_out;

  Adder #(.width(32)) adder_1 (.a(A), .b(B), .out(adder_1_out), .cin(1'b0), .cout(adder_1_cout));
  Subtractor #(.width(32)) subtractor_1 (.a(A), .b(B), .out(subtractor_1_out), .bin(1'b0), .bout(subtractor_1_bout));
  Multiplier #(.width(32)) multiplier_1 (.a(A), .b(B), .out(multiplier_1_out), .cin({32{1'b0}}));  // open: cout
  Divider #(.width(32)) divider_1 (.a(A), .b(B), .out(divider_1_out), .upper({32{1'b0}}), .rem(divider_1_rem));
  Comparator #(.width(32)) comparator_1 (.a(A), .b(B), .gt(is), .eq(is_2));  // open: lt
  Shifter #(.width(32)) shifter_1 (.in(A), .\dist (B[4:0]), .out(shifter_1_out));
  Shifter #(.width(32), .shift("lr")) shifter_2 (.in(A), .\dist (B[4:0]), .out(shifter_2_out));
  Shifter #(.width(32), .shift("ar")) shifter_3 (.in(A), .\dist (B[4:0]), .out(shifter_3_out));
  assign not_1_out = ~B;  // NOT_Gate not_1, 32 bits wide
  assign and_1_out = A & B;  // AND_Gate and_1, 32 bits wide
  assign or_1_out = A | B;  // OR_Gate or_1, 32 bits wide
  Multiplexer #(.select(4), .enable("false")) multiplexer_1 (
    .in0(adder_1_cout), .in1(subtractor_1_bout), .in2(1'b0), .in3(1'b0), .in4(1'b0), .in5(1'b0), .in6(1'b0),
    .in7(1'b0), .in8(1'b0), .in9(1'b0), .in10(1'b0), .in11(1'b0), .in12(1'b0), .in13(1'b0), .in14(1'b0),
    .in15(1'b0), .out(Carry), .sel(opcode));
  Multiplexer #(.select(4), .width(32), .disabled(0), .enable("false")) multiplexer_2 (
    .in0(adder_1_out), .in1(subtractor_1_out), .in2(multiplier_1_out), .in3(divider_1_out),
    .in4(divider_1_rem), .in5(B), .in6(shifter_1_out), .in7(shifter_2_out), .in8(shifter_3_out),
    .in9(not_1_out), .in10(and_1_out), .in11(or_1_out), .out(aluResult), .sel(opcode));  // open: in12, in13, in14, in15

  // Notes on the sheet:
  //   mod
endmodule

module Flags (
  input  isCmp,
  input  is,
  input  is_2,
  output flags_GT,
  output flags_E
);

  D_Flip_Flop #(.trigger("high")) d_ff_1 (.clk(isCmp), .D(is), .Q(flags_GT));  // open: Qn, preset, en, reset
  D_Flip_Flop #(.trigger("high")) d_ff_2 (.clk(isCmp), .D(is_2), .Q(flags_E));  // open: Qn, preset, en, reset
endmodule

module Memory (
  input  [31:0] MAR,
  input  marRead,
  input  [31:0] MDR,
  input  Clock,
  input  enable,
  input  mdrRead,
  input  [3:0] operation,
  output [31:0] ldResult
);

  wire not_1_out;
  wire [23:0] register_1_q;
  wire [31:0] register_2_q;

  Register #(.width(24)) register_1 (.D(MAR[25:2]), .en(marRead), .Q(register_1_q), .clk(Clock));  // open: clr
  Register #(.width(32)) register_2 (.D(MDR), .Q(register_2_q), .clk(Clock));  // open: en, clr
  not not_1 (not_1_out, operation[0]);
  RAM #(.addrWidth(24), .dataWidth(32), .bus("separate")) ram_1 (
    .addr(register_1_q), .din(register_2_q), .data(ldResult), .str(not_1_out), .sel(enable), .clk(Clock),
    .ld(operation[0]));  // open: clr
endmodule

module Register_file (
  input  Clock,
  input  Reset,
  input  [31:0] regData,
  input  [3:0] regSrc,
  input  [3:0] DisplayAddress,
  input  [3:0] opcode,
  output [31:0] regVal,
  output [31:0] DisplayD
);

  wire demultiplexer_1_out0, demultiplexer_1_out1, demultiplexer_1_out2, demultiplexer_1_out3,
       demultiplexer_1_out4, demultiplexer_1_out5, demultiplexer_1_out6, demultiplexer_1_out7,
       demultiplexer_1_out8, demultiplexer_1_out9, demultiplexer_1_out10, demultiplexer_1_out11,
       demultiplexer_1_out12, demultiplexer_1_out13, demultiplexer_1_out14, demultiplexer_1_out15,
       multiplexer_2_out, or_1_out, or_2_out, WriteEnable;
  wire [31:0] multiplexer_1_out, r0_q, r1_q, r2_q, r3_q, r4_q, r5_q, r6_q, r7_q, r8_q, r9_q, r10_q, r11_q,
       r12_q, r13_q, r14_q, r15_q;

  Demultiplexer #(.select(4), .disabled(0), .enable("false")) demultiplexer_1 (
    .out0(demultiplexer_1_out0), .out1(demultiplexer_1_out1), .out2(demultiplexer_1_out2),
    .out3(demultiplexer_1_out3), .out4(demultiplexer_1_out4), .out5(demultiplexer_1_out5),
    .out6(demultiplexer_1_out6), .out7(demultiplexer_1_out7), .out8(demultiplexer_1_out8),
    .out9(demultiplexer_1_out9), .out10(demultiplexer_1_out10), .out11(demultiplexer_1_out11),
    .out12(demultiplexer_1_out12), .out13(demultiplexer_1_out13), .out14(demultiplexer_1_out14),
    .out15(demultiplexer_1_out15), .in(WriteEnable), .sel(regSrc));
  Multiplexer #(.width(32), .enable("false")) multiplexer_1 (
    .in0(regData), .in1(32'h3fffffc), .out(multiplexer_1_out), .sel(Reset));
  or or_1 (or_1_out, demultiplexer_1_out14, Reset);
  not not_1 (WriteEnable, opcode[0]);
  Multiplexer #(.enable("false")) multiplexer_2 (.in0(or_2_out), .out(multiplexer_2_out), .sel(1'b0));  // open: in1
  or or_2 (or_2_out, Clock, Reset);
  Register #(.width(32)) r0 (.D(regData), .en(demultiplexer_1_out0), .Q(r0_q), .clk(Clock), .clr(Reset));
  Register #(.width(32)) r1 (.D(regData), .en(demultiplexer_1_out1), .Q(r1_q), .clk(Clock), .clr(Reset));
  Register #(.width(32)) r2 (.D(regData), .en(demultiplexer_1_out2), .Q(r2_q), .clk(Clock), .clr(Reset));
  Register #(.width(32)) r3 (.D(regData), .en(demultiplexer_1_out3), .Q(r3_q), .clk(Clock), .clr(Reset));
  Register #(.width(32)) r4 (.D(regData), .en(demultiplexer_1_out4), .Q(r4_q), .clk(Clock), .clr(Reset));
  Register #(.width(32)) r5 (.D(regData), .en(demultiplexer_1_out5), .Q(r5_q), .clk(Clock), .clr(Reset));
  Register #(.width(32)) r6 (.D(regData), .en(demultiplexer_1_out6), .Q(r6_q), .clk(Clock), .clr(Reset));
  Register #(.width(32)) r7 (.D(regData), .en(demultiplexer_1_out7), .Q(r7_q), .clk(Clock), .clr(Reset));
  Register #(.width(32)) r8 (.D(regData), .en(demultiplexer_1_out8), .Q(r8_q), .clk(Clock), .clr(Reset));
  Register #(.width(32)) r9 (.D(regData), .en(demultiplexer_1_out9), .Q(r9_q), .clk(Clock), .clr(Reset));
  Register #(.width(32)) r10 (.D(regData), .en(demultiplexer_1_out10), .Q(r10_q), .clk(Clock), .clr(Reset));
  Register #(.width(32)) r11 (.D(regData), .en(demultiplexer_1_out11), .Q(r11_q), .clk(Clock), .clr(Reset));
  Register #(.width(32)) r12 (.D(regData), .en(demultiplexer_1_out12), .Q(r12_q), .clk(Clock), .clr(Reset));
  Register #(.width(32)) r13 (.D(regData), .en(demultiplexer_1_out13), .Q(r13_q), .clk(Clock), .clr(Reset));
  Register #(.width(32)) r14 (.D(multiplexer_1_out), .en(or_1_out), .Q(r14_q), .clk(multiplexer_2_out));  // open: clr
  Register #(.width(32)) r15 (.D(regData), .en(demultiplexer_1_out15), .Q(r15_q), .clk(Clock), .clr(Reset));
  Multiplexer #(.select(4), .width(32), .disabled(0)) multiplexer_3 (
    .in0(r0_q), .in1(r1_q), .in2(r2_q), .in3(r3_q), .in4(r4_q), .in5(r5_q), .in6(r6_q), .in7(r7_q),
    .in8(r8_q), .in9(r9_q), .in10(r10_q), .in11(r11_q), .in12(r12_q), .in13(r13_q), .in14(r14_q),
    .in15(r15_q), .out(regVal), .sel(regSrc), .en(opcode[0]));
  Multiplexer #(.select(4), .width(32), .disabled(0), .enable("false")) multiplexer_4 (
    .in0(r0_q), .in1(r1_q), .in2(r2_q), .in3(r3_q), .in4(r4_q), .in5(r5_q), .in6(r6_q), .in7(r7_q),
    .in8(r8_q), .in9(r9_q), .in10(r10_q), .in11(r11_q), .in12(r12_q), .in13(r13_q), .in14(r14_q),
    .in15(r15_q), .out(DisplayD), .sel(DisplayAddress));

  // Other names for the same wires on the sheet: ReadEnable = opcode[0]
endmodule

module Immediate_Unit (
  input  [17:0] imm,
  output [31:0] immx
);

  wire [31:0] bit_extender_1_out, bit_extender_2_out, shifter_1_out;

  assign bit_extender_1_out = {{16{1'b0}}, imm[15:0]};  // Bit_Extender bit_extender_1
  assign bit_extender_2_out = {{16{imm[15]}}, imm[15:0]};  // Bit_Extender bit_extender_2
  Shifter #(.width(32)) shifter_1 (.in(bit_extender_1_out), .\dist (5'b10000), .out(shifter_1_out));
  Multiplexer #(.select(2), .width(32), .enable("false")) multiplexer_1 (
    .in0(bit_extender_2_out), .in1(bit_extender_1_out), .in2(shifter_1_out), .out(immx), .sel(imm[17:16]));  // open: in3

  // Notes on the sheet:
  //   modifier bits
  //   high
  //   default
  //   unsigned
endmodule

module MicroControl_Unit (
  input  [1:0] pc,
  input  ir,
  input  I,
  input  rd,
  input  rs1,
  input  rs2,
  input  immx,
  input  branchTarget,
  input  [1:0] regSrc,
  input  [1:0] regData,
  input  [1:0] regVal,
  input  Clock,
  input  [5:0] args,
  input  [1:0] transfer,
  input  [1:0] A,
  input  [1:0] B,
  input  [31:0] microImm,
  input  flags_E,
  input  flags_GT,
  input  [1:0] aluResult,
  input  [31:0] readbusVal,
  input  [1:0] mar,
  input  [1:0] mdr,
  input  [1:0] ldResult,
  input  [4:0] opcode,
  input  [31:0] microImm_readBusVal
);

  wire isMBranch, undriven;
  wire [1:0] microfetch;
  wire [9:0] mbranchTarget;
  wire [11:0] microimmediate;
  wire [23:0] adder_1_out, bit_extender_1_out, micropc, multiplexer_2_out, toMicroPC, undriven_2;

  Register #(.width(24), .trigger("falling")) u_microPC (.D(toMicroPC), .Q(micropc), .clk(undriven));  // open: en, clr
  assign bit_extender_1_out = {{14{1'b0}}, mbranchTarget};  // Bit_Extender bit_extender_1
  Multiplexer #(.select(2), .width(24), .enable("false")) multiplexer_1 (
    .in0(undriven_2), .in1(adder_1_out), .in2(bit_extender_1_out), .in3(multiplexer_2_out), .out(toMicroPC),
    .sel(microfetch));
  Multiplexer #(.width(24), .enable("false")) multiplexer_2 (
    .in0(adder_1_out), .in1(bit_extender_1_out), .out(multiplexer_2_out), .sel(isMBranch));
  Adder #(.width(24)) adder_1 (.a(micropc), .b(24'h1), .out(adder_1_out));  // open: cin, cout
  switch switch_1 (.opcode(opcode), .in_1(undriven_2));
  ROM #(.addrWidth(24), .dataWidth(29)) rom_1 (
    .addr(micropc),
    .data({ldResult, mdr, mar, aluResult, flags_GT, flags_E, B, A, regVal, regData, regSrc, branchTarget, immx, rs2, rs1, rd, I, ir, pc}));  // open: sel
  ROM #(.addrWidth(24), .dataWidth(28)) rom_2 (
    .addr(micropc), .data({args, mbranchTarget, microimmediate}));  // open: sel
  assign microImm = {{20{1'b0}}, microimmediate};  // Bit_Extender bit_extender_2
  ROM #(.addrWidth(24), .dataWidth(4)) rom_3 (.addr(micropc), .data({microfetch, transfer}));  // open: sel
  Comparator #(.width(32), .mode("unsigned")) comparator_1 (
    .a(microImm), .b(readbusVal), .eq(isMBranch));  // open: gt, lt
  Adder #(.width(32)) adder_2 (.a(microImm), .b(readbusVal), .out(microImm_readBusVal));  // open: cin, cout

  // Notes on the sheet:
  //   Control ROMs
  //   Decision ROM
endmodule

module switch (
  input  [23:0] in_1,
  input  [4:0] opcode
);

  Multiplexer #(.select(5), .width(24), .enable("false")) multiplexer_1 (
    .out(in_1), .sel(opcode));  // open: in0, in1, in2, in3, in4, in5, in6, in7, in8, in9, in10, in11, in12, in13, in14, in15, in16, in17, in18, in19, in20, in21, in22, in23, in24, in25, in26, in27, in28, in29, in30, in31
endmodule
